// Logisim project Sumador 1 Bit Completo.circ as structural Verilog: 3 circuits, main circuit Sumador 9 Bits
module DEMO__sumador_completo (
  input  A,
  input  B,
  input  C,
  output Suma,
  output Acarreo
);

  wire nand_1_out, nand_2_out, nand_3_out, nand_4_out, nand_5_out, nand_6_out, nand_7_out;

  nand nand_1 (nand_1_out, A, B);
  nand nand_2 (nand_2_out, A, nand_1_out);
  nand nand_3 (nand_3_out, nand_1_out, B);
  nand nand_4 (nand_4_out, nand_2_out, nand_3_out);
  nand nand_5 (nand_5_out, nand_4_out, C);
  nand nand_6 (nand_6_out, nand_4_out, nand_5_out);
  nand nand_7 (nand_7_out, nand_5_out, C);
  nand nand_8 (Acarreo, nand_5_out, nand_1_out);
  nand nand_9 (Suma, nand_6_out, nand_7_out);

  // Notes on the sheet:
  //   AxB
  //   [AxB]xA
  //   [AxB]xB
  //   ( [AxB]xB ) x ( [AxB]xA )
  //   [( [AxB]xB ) x ( [AxB]xA )]xC
  //   ([ [( [AxB]xB ) x ( [AxB]xA )]xC ] x C)
  //   [( [AxB]xB ) x ( [AxB]xA )]xC
  //   x [ ( [AxB]xB ) x ( [AxB]xA ) ]
  //   [ [( [AxB]xB ) x ( [AxB]xA )]xC ] x C
  //   x (AxB)
endmodule

module DEMO__sumador (
  input  A,
  input  B,
  output Suma,
  output Acarreo
);

  wire nand_1_out, nand_2_out, nand_3_out;

  nand nand_1 (nand_1_out, A, B);
  nand nand_2 (nand_2_out, nand_1_out, A);
  nand nand_3 (nand_3_out, nand_1_out, B);
  not nand_4 (Acarreo, nand_1_out);  // NAND_Gate
  nand nand_5 (Suma, nand_2_out, nand_3_out);

  // Notes on the sheet:
  //   AxB
  //   [AxB]xA
  //   [AxB]xB
  //   [AxB]x[AxB]
endmodule

module Sumador_9_Bits (
  input  Init__1,
  input  _1,
  input  in_3,
  input  _2,
  input  in_5,
  input  _4,
  input  in_7,
  input  _8,
  input  in_9,
  output _1_2,
  output _2_2,
  output _4_2,
  output _8_2,
  output _16
);

  wire demo_sumador_completo_1_acarreo, demo_sumador_completo_2_acarreo, demo_sumador_completo_3_acarreo;

  DEMO__sumador_completo demo_sumador_completo_1 (
    .A(in_3), .B(_1), .C(Init__1), .Suma(_1_2), .Acarreo(demo_sumador_completo_1_acarreo));
  DEMO__sumador_completo demo_sumador_completo_2 (
    .A(_2), .B(in_5), .C(demo_sumador_completo_1_acarreo), .Suma(_2_2),
    .Acarreo(demo_sumador_completo_2_acarreo));
  DEMO__sumador_completo demo_sumador_completo_3 (
    .A(in_7), .B(_4), .C(demo_sumador_completo_2_acarreo), .Suma(_4_2),
    .Acarreo(demo_sumador_completo_3_acarreo));
  DEMO__sumador_completo demo_sumador_completo_4 (
    .A(in_9), .B(_8), .C(demo_sumador_completo_3_acarreo), .Suma(_8_2), .Acarreo(_16));
endmodule
