// Logisim project Sumador 1 Bit NAND.circ as structural Verilog: 1 circuit, main circuit main
module main (
  input  A,
  input  B,
  output out_3,
  output out_4
);

  wire nand_1_out, nand_2_out, nand_3_out;

  nand nand_1 (nand_1_out, A, B);
  nand nand_2 (nand_2_out, nand_1_out, A);
  nand nand_3 (nand_3_out, nand_1_out, B);
  not nand_4 (out_4, nand_1_out);  // NAND_Gate
  nand nand_5 (out_3, nand_2_out, nand_3_out);
endmodule
